# Fritzing sketch SaarHackathon4_StMartinsLed (saved by Fritzing 1.0.1rc)

parts:
  MH-ET_LIVE_ESP32_DEVKIT1 = MH-ET LIVE ESP32 DEVKIT 38 pins
  Part3 = 12 NeoPixel Ring [part_number=1643]

nets:
  5V: MH-ET_LIVE_ESP32_DEVKIT1.5V, Part3.VDD
  GND: MH-ET_LIVE_ESP32_DEVKIT1.GND, Part3.GND
  N1: MH-ET_LIVE_ESP32_DEVKIT1.IO16, Part3.IN

custom parts:
  MH-ET LIVE ESP32 DEVKIT 38 pins: http://mh.nodebb.com/topic/2/mh-et-live-esp32-devkit
  12 NeoPixel Ring: 12 ultra bright smart LED NeoPixels are arranged in a circle with 1.5" (37mm) outer diameter. The rings are 'chainable' - connect the output pin of one to the input pin of another. Use only one microcontroller pin to control as many as you can chain together! Each LED is addressable as the driver chip is inside the LED. Each one has ~18mA constant current drive so the color will be very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
